# Fritzing sketch button (saved by Fritzing 0.9.3b)

parts:
  U2 = NodeMCU V1.0
  S1 = Pushbutton [package="[THT]"]

nets:
  N1: U2.D1, U2.GND, U2.D5, U2.D7, S1.Pin_1, S1.Pin_2, S1.Pin_3, S1.Pin_4

custom parts:
  NodeMCU V1.0: ESP8266 based NodeMCU V1.0
