# Fritzing sketch hc-sr04 (saved by Fritzing 0.9.3b)

parts:
  U2 = NodeMCU V1.0
  Part1 = SRF05 Ultrasonic Rangefinder

nets:
  N1: U2.D1, U2.D5, U2.D6, U2.D7, U2.3V3, Part1.Trig, Part1.Echo
  VIN: U2.Vin, Part1.VCC
  GND: U2.GND, Part1.GND

custom parts:
  NodeMCU V1.0: ESP8266 based NodeMCU V1.0
