# Fritzing sketch neopixels (saved by Fritzing 0.9.3b)

parts:
  Part2 = NeoPixel Stick [part_number=1426]
  U2 = NodeMCU V1.0

nets:
  +5V: Part2.+5V, U2.Vin
  N1: Part2.DATAIN, U2.D1, U2.D5, U2.GND#13
  N2: Part2.GND, U2.GND#16

custom parts:
  NeoPixel Stick: Make your own little LED strip arrangement with this stick of NeoPixel LEDs. We crammed 8 of the tiny 5050 (5mm x 5mm) smart RGB LEDs onto a PCB with mounting holes and a chainable design. Use only one microcontroller pin to control as many as you can chain together! Each LED is addressable as the driver chip is inside the LED. Each one has ~18mA constant current drive so the color will be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
  NodeMCU V1.0: ESP8266 based NodeMCU V1.0
