# Fritzing sketch rgb-lamp-esp12e (saved by Fritzing 0.9.3b)
breadboards: 1

parts:
  ESP1 = ESP 12E
  CP1 = CP2102 D-SUN
  LED1 = RGB LED (com. cathode, rgb) [package="5 mm [THT]"]

nets:
  N1: ESP1.TX0, CP1.RXD
  N2: ESP1.RX0, CP1.TXD
  GND: ESP1.GPIO0, ESP1.GPIO15, ESP1.GND, ESP1.MOSI, CP1.GND, LED1.common_cathode
  N3: ESP1.MISO, ESP1.VCC, ESP1.EN, CP1.VCC3V3
  N4: ESP1.GPIO13, LED1.blue_anode
  N5: ESP1.GPIO12, LED1.green_anode
  N6: ESP1.GPIO14, LED1.red_anode

custom parts:
  ESP 12E: ESP 12e module with spi interface and wifi connection
  CP2102 D-SUN: USB to Serial
