# Fritzing sketch rgb-lamp (saved by Fritzing 0.9.3b)

parts:
  U2 = NodeMCU V1.0
  LED1 = RGB LED (com. cathode, rbg) [color="Red (633nm)" package="5 mm [THT]"]

nets:
  N1: U2.D1, U2.GND, U2.D5, U2.D6, U2.D7, LED1.red_anode, LED1.common_cathode, LED1.blue_anode, LED1.green_anode

custom parts:
  NodeMCU V1.0: ESP8266 based NodeMCU V1.0
